// Logisim project digital_tube_abcdfg.circ as structural Verilog
module main (
  input  in_1,
  input  [3:0] in_2
);

  wire [7:0] digital_tube_1_display;

  digital_tube digital_tube_1 (.en(in_1), .dat(in_2), .display(digital_tube_1_display));
  _7_Segment_Display u_7_segment_display_1 (
    .g(digital_tube_1_display[1]), .f(digital_tube_1_display[2]), .a(digital_tube_1_display[7]),
    .b(digital_tube_1_display[6]), .e(digital_tube_1_display[3]), .d(digital_tube_1_display[4]),
    .c(digital_tube_1_display[5]), .dp(digital_tube_1_display[0]));
endmodule

// VHDL entity digital_tube, as the project stores it:
library ieee;
use ieee.std_logic_1164.all;
use ieee.std_logic_arith.all;
use ieee.std_logic_unsigned.all;

entity digital_tube is
    port(
        en      :in std_logic;
        dat     :in std_logic_vector(3 downto 0);
        display :out std_logic_vector(7 downto 0)
    );
end entity digital_tube;

architecture bhv of digital_tube is
begin
    process(en,dat)
    begin
        if en='0' then
            display <= "ZZZZZZZZ";
          else
            case dat is
                when "0000" => display <= "11101110";
                when "0001" => display <= "00111110";
                when "0010" => display <= "10011100";
                when "0011" => display <= "01111010";
                when "0100" => display <= "10001110";
                when "0101" => display <= "11110110";
                when others => display <= "00000000";
            end case;
        end if;
    end process;
end architecture bhv;
