// Logisim project p5.circ as structural Verilog
module main (
  input  in_1,
  input  [12:0] in_2
);

  wire [7:0] digital_tube_vt_1_display;

  digital_tube_vt digital_tube_vt_1 (.en(in_1), .vt(in_2), .display(digital_tube_vt_1_display));
  _7_Segment_Display u_7_segment_display_1 (
    .g(digital_tube_vt_1_display[1]), .f(digital_tube_vt_1_display[2]), .a(digital_tube_vt_1_display[7]),
    .b(digital_tube_vt_1_display[6]), .e(digital_tube_vt_1_display[3]), .d(digital_tube_vt_1_display[4]),
    .c(digital_tube_vt_1_display[5]), .dp(digital_tube_vt_1_display[0]));
endmodule

// VHDL entity digital_tube_vt, as the project stores it:
library ieee;
use ieee.std_logic_1164.all;
use ieee.std_logic_arith.all;
use ieee.std_logic_unsigned.all;

entity digital_tube_vt is
    port(
        en      :in std_logic;
        vt      :in std_logic_vector(13 downto 1);
        display :out std_logic_vector(7 downto 0)
    );
end entity digital_tube_vt;

architecture bhv of digital_tube_vt is
begin
    process(en,vt)
    variable sum:integer range 0 to 13;
    begin
        sum:= 0;
        for i in 1 to 13 loop
            if (vt(i)='1') then
                sum:= sum + 1;
            end if;
        end loop;

        if en='0' then
            display <= "ZZZZZZZZ";
          else
            case sum is
                when 0 => display <= "11111100";
                when 1 => display <= "01100000";
                when 2 => display <= "11011010";
                when 3 => display <= "11110010";
                when 4 => display <= "01100110";
                when 5 => display <= "10110110";
                when 6 => display <= "10111110";
                when 7 => display <= "11100000";
                when 8 => display <= "11111110";
                when 9 => display <= "11100110";
                when 10 => display <= "11101110";
                when 11 => display <= "00111110";
                when 12 => display <= "10011100";
                when 13 => display <= "01111010";
                when others => display <= "00000000";
            end case;
        end if;
    end process;
end architecture bhv;
